# Fritzing sketch RFID_servo_schematic (saved by Fritzing 0.9.3b)

parts:
  U1 = NodeMCU V1.0
  RFID_MFRC522 = RFID-RC522-v2
  Sevo_Motor = Basic Servo

nets:
  N1: U1.D1, Sevo_Motor.pulse
  N2: U1.D4, RFID_MFRC522.RST
  3V3: U1.3V3, RFID_MFRC522.3_3V, Sevo_Motor.vcc
  GND: U1.GND, RFID_MFRC522.GND, Sevo_Motor.gnd
  N3: U1.D5, RFID_MFRC522.SCK
  N4: U1.D6, RFID_MFRC522.MISO
  N5: U1.D7, RFID_MFRC522.MOSI
  N6: U1.D8, RFID_MFRC522.SDA

custom parts:
  NodeMCU V1.0: ESP8266 based NodeMCU
  RFID-RC522-v2: A simple China made RFID-RC522 Reader; do check the pin labels, as this is a MFRC522 based clone.
