# Fritzing sketch regulator_schematic (saved by Fritzing 0.9.3b)

parts:
  U3 = NodeMCU V1.0
  Optocoupler = Optocoupler [package=THT]
  Zener_Diode = Zener Diode [part_number=1N4732A breakdown_voltage=3.6V package="300 mil [THT]"]
  2_2uF = Electrolytic Capacitor [capacitance=100μF package="0807 [SMD, electrolytic]"]
  220nF = Ceramic Capacitor [capacitance="100 nF" package="0805 [SMD, multilayer]"]
  IRF830 = Basic FET N-Channel [package="TO220 [THT]"]
  1N4007 = Diode [package=diode-1n4148]
  Bridge_Rectifier = DB107 [package=THT]
  220 = Resistor [tolerance=±5% resistance=220 package="0805 [SMD]"]
  330 = Resistor [tolerance=±5% resistance=220 package="0805 [SMD]"]
  33k = Resistor [tolerance=±5% resistance=220 package="0805 [SMD]"]
  33k_2 = Resistor [tolerance=±5% resistance=220 package="0805 [SMD]"]
  22k = Resistor [tolerance=±5% resistance=220 package="0805 [SMD]"]
  AC_230V_Supply = AC Power [voltage=5 frequency=60]
  LOAD = Resistor [tolerance=±5% resistance=220 package=THT]

nets:
  N1: U3.GND, Optocoupler.Pin_2
  N2: U3.D7, 330.Pin_0
  N3: Optocoupler.Pin_1, 330.Pin_1
  N4: Optocoupler.Pin_4, IRF830.gate, 22k.Pin_0
  N5: Optocoupler.Pin_5, Zener_Diode.cathode, 2_2uF.+, 33k_2.Pin_1
  N6: Zener_Diode.anode, 2_2uF.-, 220nF.0, IRF830.source, Bridge_Rectifier.Pin_4, 22k.Pin_1
  N7: 220nF.1, 220.Pin_0, 33k.Pin_1
  N8: IRF830.drain, 1N4007.A, Bridge_Rectifier.Pin_3
  N9: 1N4007.C, 220.Pin_1
  N10: Bridge_Rectifier.Pin_1, LOAD.Pin_0
  N11: Bridge_Rectifier.Pin_2, AC_230V_Supply.V+
  N12: 33k.Pin_0, 33k_2.Pin_0
  N13: AC_230V_Supply.V-, LOAD.Pin_1

custom parts:
  NodeMCU V1.0: ESP8266 based NodeMCU
  DB107: Bridge rectifier
