# Fritzing sketch sensors_schematic (saved by Fritzing 0.9.3b)

parts:
  NodeMCU = NodeMCU V1.0
  Arduino_UNO = Arduino Uno (Rev3) - ICSP
  Accelerometer = Triple Axis Accelerometer Breakout - ADXL335
  Light_intensity_Sensor = Ambient Light Sensor (TEMT6000 Breakout Board)
  Temperature-Humidity_sensor = DHT11 Humitidy and Temperature Sensor

nets:
  N1: NodeMCU.RX, Arduino_UNO.D5_PWM
  N2: NodeMCU.TX, Arduino_UNO.D4
  N3: Arduino_UNO.A0, Light_intensity_Sensor.S
  N4: Arduino_UNO.A1, Accelerometer.XOUT
  N5: Arduino_UNO.A2, Accelerometer.YOUT
  N6: Arduino_UNO.A3, Accelerometer.ZOUT
  N7: Arduino_UNO.D6_PWM, Temperature-Humidity_sensor.DATA
  VCC: Arduino_UNO.3V3, Accelerometer.VCC, Light_intensity_Sensor.VCC, Temperature-Humidity_sensor.VDD
  GND: Arduino_UNO.GND, Light_intensity_Sensor.GND, Temperature-Humidity_sensor.GND

custom parts:
  NodeMCU V1.0: ESP8266 based NodeMCU
  DHT11 Humitidy and Temperature Sensor: DHT11 Humidity and Temperature Sensor
