# Fritzing sketch smartPlug_only_schematic (saved by Fritzing 0.9.3b)

parts:
  U1 = NodeMCU V1.0
  Green_LED = smd LED [color="Red (633nm)" package="0805 [SMD]"]
  Red_LED = smd LED [color="Red (633nm)" package="0805 [SMD]"]
  BC547 = TRANSISTOR_NPN [package=to-92]
  SPDT = SWITCH_SPDT [package=kps-1290]
  100uF = Electrolytic Capacitor [capacitance=1000μF package="1010 [SMD, electrolytic]"]
  R1 = Resistor [tolerance=±5% resistance=220 package="0805 [SMD]"]
  R2 = Resistor [tolerance=±5% resistance=220 package="0805 [SMD]"]
  10k = Resistor [tolerance=±5% resistance=220 package="0805 [SMD]"]
  S116S02 = RELAY-SOLIDSTATE [package=relay-s108t02]
  5V_DC_Supply = DC Power [voltage=5]

nets:
  N1: U1.D0, R1.Pin_1
  N2: U1.D1, R2.Pin_0
  N3: U1.D2, SPDT.P
  N4: U1.D3, SPDT.O
  N5: U1.D5, 10k.Pin_1
  N6: U1.D6, SPDT.S
  GND: Green_LED.cathode, Red_LED.cathode, BC547.E, 100uF.-, 5V_DC_Supply.V-
  N7: Green_LED.anode, R2.Pin_1
  N8: Red_LED.anode, R1.Pin_0
  N9: BC547.B, 10k.Pin_0
  N10: BC547.C, S116S02.-
  N11: 100uF.+, S116S02.+, 5V_DC_Supply.V+

notes:
  AC Connections
  Regulator Circuit

custom parts:
  NodeMCU V1.0: ESP8266 based NodeMCU
